# Fritzing sketch Solar Design (saved by Fritzing 0.9.6b)
stripboards: 1

parts:
  U1 = ESP32-38PinWide [part_number=ESP32-38PinWide]
  TP1 = TP4056 [chip_label=TP4056 package="DIP (Dual Inline) [THT]"]
  REG1 = LD33 Low-Dropout Voltage Regulator
  C1 = Capacitor Polarized [package=nippon_f80]
  C2 = Ceramic Capacitor [capacitance=100nF voltage=35V package="100 mil [THT, multilayer]"]
  JP1 = Header 2 [package=jst-2-pth-ns]
  JP2 = Header 2 [package=jst-2-pth-ns]
  R1 = Resistor [tolerance=±5% resistance=1M package="2010 [SMD]"]
  R2 = Resistor [tolerance=±5% resistance=100k package="2010 [SMD]"]
  R3 = Resistor [tolerance=±5% resistance=1M package="2010 [SMD]"]
  R4 = Resistor [tolerance=±5% resistance=100k package="2010 [SMD]"]
  Part1 = BH1750
  M1 = BME280

nets:
  VCC: U1.3.3, REG1.Vout, C1.+, C2.1, Part1.VCC, M1.VIN
  N1: U1.GPIO32, R1.Pin_1, R2.Pin_0
  N2: U1.GPIO33, R3.Pin_1, R4.Pin_0
  GND: U1.GND, TP1.pin6, REG1.GND, C1.-, C2.0, R2.Pin_1, R4.Pin_1, Part1.GND, M1.GND
  N3: U1.GPIO21, Part1.SDA, M1.SDA
  N4: U1.GPIO22, Part1.SCL, M1.SCL
  N5: TP1.pin1, JP1.1, R1.Pin_0
  N6: TP1.pin2, JP1.2
  N7: TP1.pin3, REG1.Vin
  N8: TP1.pin4, JP2.1, R3.Pin_0
  N9: TP1.pin5, JP2.2

custom parts:
  ESP32-38PinWide: Generic 38-Pin ESP32 with wide format (only access to one side of pins on a breadboard) based on Stephen Lilley's HiLetgo ESP-WROOM-32 ESP32 ESP-32S Development Board.
  TP4056: A DIP stand-in part for whatever IC you want. With 6 pins on a 300mil dual inline package (DIP) footprint.
  BH1750: Light Sensor
  BME280: Temperature Humidity Barometric presure Sensor
